# Fritzing sketch Navbot (saved by Fritzing 0.9.3b)
circuit board: 8.46667cm x 5.64444cm
breadboards: 1

parts:
  Part1 = Arduino Uno (Rev3)
  M2 = DC Motor
  J1 = Infrared Proximity Sensor
  J2 = Infrared Proximity Sensor
  M3 = DC Motor
  IC1 = L293D [package=THT]

nets:
  N1: Part1.A0, J1.Vcc
  N2: Part1.A1, J2.Vcc
  N3: Part1.D9_PWM, IC1.In_2
  N4: Part1.D10_PWM/SS, IC1.In_1
  N5: Part1.D5_PWM, IC1.In_4
  N6: Part1.D6_PWM, IC1.In_3
  N7: Part1.5V, J1.Vout, J2.Vout, IC1.Enable_1, IC1.+Vmotor, IC1.Enable_2, IC1.+V
  GND: Part1.GND, J1.GND, J2.GND, IC1.0V
  N8: M2.pin_1, IC1.Out_4_(_Controlled_by_Enable_2_)
  N9: M2.pin_2, IC1.Out_3_(_Controlled_by_Enable_2_)
  N10: M3.pin_1, IC1.Out_2_(_Controlled_by_Enable_1_)
  N11: M3.pin_2, IC1.Out_1_(_Controlled_by_Enable_1_)

// code stored in the sketch: Arduino_Navbot_Rev_frit.ino
//#include <EEPROM.h>


int f = 0;
float dw = 02.82; // CHANGE IT FOR METRES CONVERSION
int val_new;
int val_old;
int clicks = 0;
int val_new2;
int val_old2;
int clicks2 = 0;
float dis = 0.00;
float dt_p1_d = 0.00; // 
float dt_p1_a = 0.00; //
//float be_p1_d = 0.00; //
float be_p1_a = 0.00; //
float be_p1_a_be = 0.00; 
float it_p1_a_it = 0.00; 
float it_p1_d = 0.00; //
float be_it_d = 0.00; //
float p1_be_h_1 = 0.00;
float p1_be_h_2 = 0.00;
float p1_be_p1 = 0.00;
float ang_1 = 0.00; 
float it_p1_a = 0.00;
float p1_trig_1 = 0.00;
float dis_1 = 0.00;
float dis_2 = 0.00;
float dis_3 = 0.00;
float dis_4 = 0.00;
float dis_5 = 0.00;
float dis_6 = 0.00;
float dis_7 = 0.00;
float dt_it_d = 0.00; //
int dir = 0; //
#define s1 A0
#define s2 A1
#define MTR_R 9
#define MTR_L 5
int clk1 = 0;
int clk2 = 0;
int v_n = 7;
int v_n2 = 7;
int v_o = 7;
int v_o2 = 7;
int dis1 = 0;
int dis2 = 0;
int fdis = 0;
int av = 0;
int t = 0;
int d = 0;
int d2 = 0;
int av2 = 0;
int deg1 = 0;
int deg2 = 0;
void setup()
{

  pinMode(MTR_R, OUTPUT);
pinMode(MTR_L, OUTPUT);
//digitalWrite(MTR_R_1, 1);
//digitalWrite(MTR_R_2, 0);
//digitalWrite(MTR_L_1, 1);
//(MTR_L_2, 0);
 
  pinMode(A0, INPUT);
  pinMode(A1, INPUT);
 Serial.begin(9600);
 //getCode();
dt_p1_d = 8;
dt_p1_a = 7;
be_p1_a = 51;
it_p1_d = 10;
it_p1_a = 5;
be_it_d = 12 ;
dt_it_d = 3;
dir = 1;


pinMode(13, OUTPUT);

 }

void loop()
{
// f = millis() / 1000;
  dis = 0;
digitalWrite(MTR_R, 1);
  digitalWrite(MTR_L, 1);
 // digitalWrite(MTR_L_1, 1);
  //digitalWrite(MTR_L_2, 0);
while (cmp(be_it_d, dis) == 0){
  dis = ((getClk(1) + getClk(2)) / 2) * dw;  
} 
digitalWrite(MTR_R, 1);
  digitalWrite(MTR_L, 1);
 // digitalWrite(MTR_L_1, 0);
 // digitalWrite(MTR_L_2, 0);
  delay(1000);
   trn90(dir);
   delay(1000);
  digitalWrite(MTR_R, 1);
  digitalWrite(MTR_L, 1);
 // digitalWrite(MTR_L_1, 1);
 // digitalWrite(MTR_L_2, 0);
 dis = 0;
 clicks = 0;
 clicks2 = 0;
while (cmp(dt_it_d, dis) == 0){
  dis = ((getClk(1) + getClk(2)) / 2) * dw;  
}
digitalWrite(MTR_R, 0);
  digitalWrite(MTR_L, 0);
 // digitalWrite(MTR_L_1, 0);
  //digitalWrite(MTR_L_2, 0);
  while(1)
  {
digitalWrite(13, HIGH);
delay(1000);
digitalWrite(13, LOW);
delay(1000);
  }
}

 
 
 //delay(600);
//Serial.println(dis_2);
// Serial.println(be_it_d);
// Serial.println(cmp(be_it_d, dis_2));
  
  

//Serial.println(dis);
//dis_1 = be_it_d - dis;
//dis_2 = sqrt((square(dis_1)) + (square(be_it_d)));
//Serial.println(getClk(1));
 


int getClk(int a)
{
 // while(1){
   val_new = digitalRead(A0);
 val_new2 = digitalRead(A1);
  if (a == 1)
  {
  if (val_new != val_old) { // left
      clicks++;
      val_old = val_new;
  }
  return clicks;
    
    //Serial.println(clicks);
  }
   
  
  else if (a==2){
  
  if (val_new2 != val_old2) { // right
      clicks2++;
      val_old2 = val_new2;
       }
    return clicks2;
  //  Serial.println(clicks2);
    //Serial.println("");
  }
}
//}
int cmp(float a, float b)
{
  float r = 0.00f;
  r = a - b;
  if (r < 1)
  {
    return 1;
  }
  else if (r > 1)
  {
    return 0;
  }
}

void trn90(int c)
{
 int a = 0;
  int b = 0;
  int d = 0;
  int e = 0;
//  float f = 0.00;
  int a2 = 0;
  int b2 = 0;
  int d2 = 0;
  clicks = 0;
  clicks2 = 0;
  if (dir == 1)
  {
    while(cmp(26.70, d)==0)
    {
    digitalWrite(MTR_R, 1);
  //digitalWrite(MTR_R_2, 1);
  
    d = (getClk(2) * dw);
    
    if (cmp(26.70, d)==1 )
    {
    digitalWrite(MTR_R, 0);
   // digitalWrite(MTR_R_2, 0);
    }
    }
  
    
  
  }
  if (dir == 2)
  {
    while(cmp(26.70, d2)==0)
    {
      digitalWrite(MTR_L, 1);
 // digitalWrite(MTR_L_2, 0);
    d2 = (getClk(1) * dw);
    }
      if (cmp(26.70, d2)==1)
      {
        digitalWrite(MTR_L, 0);
  //digitalWrite(MTR_L_2, 0);
        
    }
  }
  digitalWrite(MTR_R, 0);
 // digitalWrite(MTR_R_2, 0);
  digitalWrite(MTR_L, 0);
 // digitalWrite(MTR_L_2, 0);
  
}
/*void getCode()
{
  float a = 0.00;
float b = 0.00;
float c = 0.00;
float d = 0.00;
float e = 0.00;
float f = 0.00;
int g = 3;
          while( !(Serial.available()));
    String v1 = Serial.readStringUntil(':');
    Serial.read(); 
    String v2 = Serial.readStringUntil(':');
    Serial.read();
    String v3 = Serial.readStringUntil(':');
    Serial.read();
    String v4 = Serial.readStringUntil(':');
    Serial.read();
    String v5 = Serial.readStringUntil(':');
    Serial.read();
    String v6 = Serial.readStringUntil(':');
    Serial.read();
    String v7 = Serial.readStringUntil('|');
    Serial.read();
   // Serial.read();
   // String v3  = Serial.readStringUntil('|');
   delay(200);
   a = v1.toFloat();
   b = v2.toFloat();
 c = v3.toFloat();
   d = v4.toFloat();
   e = v5.toFloat();
   f = v6.toFloat();
   g = v7.toInt();

    EEPROM.put(0, a);
    EEPROM.put(1, b);
    EEPROM.put(2, c);
    EEPROM.put(3, d);
    EEPROM.put(4, e);
    EEPROM.put(5, f);
    EEPROM.put(6, g);                                                                                     
}
*/
